// Digital circuit hw1_2-bit_multiplier.dig as structural Verilog
module hw1_2_bit_multiplier (
  input  A1,
  input  A0,
  input  B1,
  input  B0,
  output P0,
  output P2,
  output P1,
  output P3
);

  wire and_1_out, and_2_out, and_3_out, and_4_out, and_5_out, and_6_out, not_1_out, not_2_out, not_3_out,
       not_4_out, not_5_out, not_6_out, not_7_out, not_8_out, or_3_out, or_4_out, or_5_out, or_6_out,
       or_7_out, or_8_out, or_9_out, or_10_out;

  not not_1 (not_1_out, A1);
  not not_2 (not_2_out, A0);
  not not_3 (not_3_out, B1);
  not not_4 (not_4_out, B0);
  and and_1 (and_1_out, not_2_out, A1, B0);
  and and_2 (and_2_out, A1, not_3_out, B0);
  and and_3 (and_3_out, not_1_out, A0, B1);
  and and_4 (and_4_out, B1, A0, not_4_out);
  and and_5 (and_5_out, A1, not_2_out, B1);
  and and_6 (and_6_out, A1, not_4_out, B1);
  and and_7 (P0, A0, B0);
  or or_1 (P1, and_1_out, and_3_out, and_4_out, and_2_out);
  or or_2 (P2, and_5_out, and_6_out);
  and and_8 (P3, A1, A0, B1, B0);
  not not_5 (not_5_out, P3);
  not not_6 (not_6_out, P2);
  or or_3 (or_3_out, P3, not_5_out);
  or or_4 (or_4_out, P3, not_5_out);
  or or_5 (or_5_out, P2, not_6_out);
  or or_6 (or_6_out, P2, not_6_out);
  Seven_Seg seven_seg_1 (
    .a(not_5_out), .b(or_4_out), .c(or_3_out), .d(not_5_out), .e(not_5_out), .f(not_5_out), .g(1'b0),
    .dp(1'b0));
  not not_7 (not_7_out, P1);
  Seven_Seg seven_seg_2 (
    .a(not_6_out), .b(or_6_out), .c(or_5_out), .d(not_6_out), .e(not_6_out), .f(not_6_out), .g(1'b0),
    .dp(1'b0));
  or or_7 (or_7_out, P1, not_7_out);
  or or_8 (or_8_out, P1, not_7_out);
  not not_8 (not_8_out, P0);
  Seven_Seg seven_seg_3 (
    .a(not_7_out), .b(or_8_out), .c(or_7_out), .d(not_7_out), .e(not_7_out), .f(not_7_out), .g(1'b0),
    .dp(1'b0));
  or or_9 (or_9_out, P0, not_8_out);
  or or_10 (or_10_out, P0, not_8_out);
  Seven_Seg seven_seg_4 (
    .a(not_8_out), .b(or_10_out), .c(or_9_out), .d(not_8_out), .e(not_8_out), .f(not_8_out), .g(1'b0),
    .dp(1'b0));

  // Notes on the sheet:
  //   Partial Products Note: 
  //   How do Partial Products combine to form P0..P3?
  //   The partial products are the set of unsummed products of the binary multiplication of a1a0 * b1b0, as follows: a1b1, a1b0, a0b1, a0b0.
  //   Here specifically, the partial products result from the bitwise AND operation being used on each bit of the first operand with each bit of the second.
  //   a0b0 directly outputs to P0 from the circuit. Since there's no addition, nothing is ever carried to the second bit.
  //   a1b0 + a0b1 makes up P1, the second bit. Each can be 0 or 1, but since we're using addition there will be something carried in the event we get two ones.
  //   a1b1 makes up P2, the third bit, but not solely since now we have a possible carry from P1. If something isn't carried, leave it as a1b1. 
  //   (contd.) If something is however, we would add one to whatever value we have in the third bit, resulting in either a 1 or a 0 with a carry to the fourth bit.
  //   P3 is the fourth bit, and is made up of any carry that may have resulted from adding P2 with P1's carry. 
  //   The only case we have a value for P3 in our situation is when all inputs are 1, so all possible carries can occur. 
  //   P.S. Only P3 and P0 will have a value of 1 in this case, since P1 and P2 only ever add 2 inputs, P1 with the two partial products and P2 with one partial plus one carry from P1.
  //   To have all possible carries occur, P1 and P2 would need to add two 1s and have nothing leftover. P0 still has one as there is no carry or addition, just bitwise AND.
  //   Matthew's 2-bit Multiplier Implementation
  //   JUST FOR FUN/PROOF OF CONCEPT: 
  //   Testing implementation with 7-segment displays 
  //   for easier testing and viewing output of the multiplier.
  //   I thought it would be neat to try figuring it out.
endmodule
