// Digital circuit hw1_full_adder.dig as structural Verilog
module hw1_full_adder (
  input  A,
  input  Matthew_Eurdekian_s_Full_Adder_Implementation,
  input  B,
  input  Cin,
  output SUM,
  output Cout
);

  wire and_1_out, and_2_out, xor_1_out;

  xor xor_1 (xor_1_out, A, B);
  and and_1 (and_1_out, A, B);
  and and_2 (and_2_out, xor_1_out, Cin);
  xor xor_2 (SUM, xor_1_out, Cin);
  or or_1 (Cout, and_2_out, and_1_out);
endmodule
