// Digital circuit hw1_ripple-carry_adder.dig as structural Verilog
module hw1_ripple_carry_adder (
  input  A0,
  input  Matthew_s_Ripple_Carry_Adder_Implementation,
  input  B0,
  input  Cin,
  input  A1,
  input  B1,
  input  A2,
  input  B2,
  input  A3,
  input  B3,
  output S0,
  output C0,
  output S1,
  output C1,
  output S2,
  output C2,
  output S3,
  output Cout
);

  wire and_1_out, and_2_out, and_3_out, and_4_out, and_5_out, and_6_out, and_7_out, and_8_out, xor_1_out,
       xor_2_out, xor_3_out, xor_4_out;

  xor xor_1 (xor_1_out, A0, B0);
  and and_1 (and_1_out, A0, B0);
  xor xor_2 (xor_2_out, A1, B1);
  and and_2 (and_2_out, A1, B1);
  xor xor_3 (xor_3_out, A2, B2);
  and and_3 (and_3_out, A2, B2);
  xor xor_4 (xor_4_out, A3, B3);
  and and_4 (and_4_out, A3, B3);
  and and_5 (and_5_out, xor_1_out, Cin);
  and and_6 (and_6_out, xor_2_out, C0);
  and and_7 (and_7_out, xor_3_out, C1);
  and and_8 (and_8_out, xor_4_out, C2);
  xor xor_5 (S0, xor_1_out, Cin);
  or or_1 (C0, and_5_out, and_1_out);
  xor xor_6 (S1, xor_2_out, C0);
  or or_2 (C1, and_6_out, and_2_out);
  xor xor_7 (S2, xor_3_out, C1);
  or or_3 (C2, and_7_out, and_3_out);
  xor xor_8 (S3, xor_4_out, C2);
  or or_4 (Cout, and_8_out, and_4_out);
endmodule
